# Fritzing sketch Charging base (saved by Fritzing 0.9.3b)
breadboards: 1

parts:
  AC_to_12V_DC_converter = HLK-PM01
  N = SPST Switch [package=switch-spdt_kit]
  L = SPST Switch [package=switch-spdt_kit]
  220V_AC = Screw terminal - 2 pins [package=THT]
  ON/OFF = SPST Switch [package=switch-spdt]
  contacts_to_Radio = female pin header, 3 pins [form="♀ (female)"]
  1N5404 = Rectifier Diode [part_number=1N4001 package="300 mil [THT]"]
  To_3_Digit_voltmeter = female pin header, 3 pins [form="♀ (female)"]

nets:
  N1: AC_to_12V_DC_converter.AC#0, N.P
  N2: AC_to_12V_DC_converter.AC#1, L.P
  GND: AC_to_12V_DC_converter.-Vo, contacts_to_Radio.pin1, To_3_Digit_voltmeter.pin3
  12V: AC_to_12V_DC_converter.+Vo
  N3: N.O, 220V_AC.pin1
  N4: L.O, ON/OFF.P
  N5: 220V_AC.pin2, ON/OFF.S
  N6: contacts_to_Radio.pin2, To_3_Digit_voltmeter.pin2
  N7: contacts_to_Radio.pin3, 1N5404.cathode
  N8: 1N5404.anode, To_3_Digit_voltmeter.pin1

notes:
  Charging Base
