# Fritzing sketch FM front panel (saved by Fritzing 0.9.3b)
breadboards: 1

parts:
  V+ = Pushbutton [package=THT]
  Tune+ = Pushbutton [package=THT]
  Seek+ = Pushbutton [package=THT]
  Mem+ = Pushbutton [package=THT]
  Save = Pushbutton [package=THT]
  Reset = Pushbutton [package=THT]
  Mem- = Pushbutton [package=THT]
  Seek- = Pushbutton [package=THT]
  Tune- = Pushbutton [package=THT]
  V- = Pushbutton [package=THT]
  R1 = Resistor [tolerance=±5% resistance=680 package=THT]  # not connected
  R2 = Resistor [tolerance=±5% resistance=680 package=THT]  # not connected
  R3 = Resistor [tolerance=±5% resistance=680 package=THT]  # not connected
  R4 = Resistor [tolerance=±5% resistance=680 package=THT]  # not connected
  R5 = Resistor [tolerance=±5% resistance=680 package=THT]  # not connected
  R6 = Resistor [tolerance=±5% resistance=680 package=THT]  # not connected
  R7 = Resistor [tolerance=±5% resistance=680 package=THT]  # not connected
  R8 = Resistor [tolerance=±5% resistance=680 package=THT]  # not connected
  R9 = Resistor [tolerance=±5% resistance=680 package=THT]  # not connected
  R10 = Resistor [tolerance=±5% resistance=680 package=THT]
  20X4_LCD_I2C = LCD1602-I2C
  BT = LED - 5mm [color="Red (633nm)" package="5 mm [THT]"]
  Battery = LED - 5mm [color="Red (633nm)" package="5 mm [THT]"]
  Power = LED - 5mm [color="Red (633nm)" package="5 mm [THT]"]
  To_main_Board = female pin header, 8 pins [form="♀ (female)"]

nets:
  GND: V+.leg1, Tune+.leg1, Seek+.leg1, Mem+.leg1, Save.leg1, Reset.leg1, Mem-.leg1, Seek-.leg1, Tune-.leg1, V-.leg1, 20X4_LCD_I2C.GND, BT.cathode, Battery.cathode, Power.cathode, To_main_Board.pin6
  N1: R10.Pin_1, To_main_Board.pin1
  N2: 20X4_LCD_I2C.SDA, To_main_Board.pin7
  N3: 20X4_LCD_I2C.SCL, To_main_Board.pin8
  N4: BT.anode, To_main_Board.pin4
  N5: Battery.anode, To_main_Board.pin3
  N6: Power.anode, To_main_Board.pin2

notes:
  FM Radio Front Pannel

custom parts:
  LCD1602-I2C: A standard character display, usually with 2x16 characters. Comes in many colors with LCM1602 IIC attached.
