# Fritzing sketch Radio FM BT (saved by Fritzing 0.9.3b)
circuit board: 7cm x 10cm
breadboards: 1

parts:
  Composant1 = Arduino Nano (Rev3.0)
  On/OFF_switch = Screw terminal - 2 pins [package=THT]
  12V_Amplifier = Screw terminal - 2 pins [package=THT]
  7805 = Voltage Regulator - 5V [package="TO220 [THT]"]
  2200µF = Electrolytic Capacitor [capacitance=1µF package="100 mil [THT, electrolytic]"]
  33nF = Ceramic Capacitor [capacitance=10nF package="100 mil [THT, multilayer]"]
  D1 = Rectifier Diode [part_number=1N5404 package="300 mil [THT]"]
  Composant3 = Logic Level Converter
  3_3k = Resistor [tolerance=±5% resistance=220 part_number=R9 package=THT]
  3_3k_2 = Resistor [tolerance=±5% resistance=220 part_number=R10 package=THT]
  D2 = Rectifier Diode [part_number=1N5404 package="300 mil [THT]"]
  Q1 = NPN-Transistor [part_number=2N2222 package="TO92 [THT]"]
  Q2 = NPN-Transistor [part_number=2N2222 package="TO92 [THT]"]
  R1 = Resistor [tolerance=±5% resistance=1k package=THT]
  R2 = Resistor [tolerance=±5% resistance=47 package=THT]  # not connected
  9_6V_battery = Screw terminal - 2 pins [package=THT]
  12V_from_charge_base = Screw terminal - 2 pins [package=THT]
  contacts_to_charge_base = Header 3 [package=screwterminal-3.5mm-3_lock.007s]
  8xAA_2800mA_battery_block = 4 x AAA Battery Mount
  SI_4703 = SI470X [package=si470x]
  to_power_Amp = Header 3 [package=screwterminal-3.5mm-3_lock.007s]
  ANT1 = Antenna
  5v_to_3_3V_DC_converter = V_REG_LD1117VXX [package=78xxl]
  contacts_to_charge_base2 = Header 3 [package=screwterminal-3.5mm-3_lock.007s]
  contacts_to_charge_base3 = Header 3 [package=screwterminal-3.5mm-3_lock.007s]
  D3 = Rectifier Diode [part_number=1N5404 package="300 mil [THT]"]
  R3/R5 = Resistor [tolerance=±5% resistance=330 package=THT]  # not connected
  R3/R5_1 = Resistor [tolerance=±5% resistance=330 package=THT]  # not connected
  R3/R5_2 = Resistor [tolerance=±5% resistance=330 package=THT]  # not connected
  D6 = Header 1 [package=1x01_offset]  # not connected
  D7 = Header 1 [package=1x01_offset]  # not connected
  D8 = Header 1 [package=1x01_offset]  # not connected
  BT_led = Header 1 [package=1x01_offset]  # not connected
  Power_led = Header 1 [package=1x01_offset]  # not connected
  Battery_led = Header 1 [package=1x01_offset]  # not connected
  R6 = Resistor [tolerance=±5% resistance=6.8k package=THT]
  connector_to_front_pannel = Header 2 [package=molex-1x2_lock]
  A0 = Header 1 [package=1x01_offset]
  input_switches = Header 1 [package=1x01_offset]
  R3 = Resistor [tolerance=±5% resistance=3.9k part_number=R7 package=THT]
  R4 = Resistor [tolerance=±5% resistance=6.8k part_number=R8 package=THT]  # not connected
  supply_voltage = Header 1 [package=1x01_offset]
  To_supply_voltage = Header 1 [package=1x01_offset]  # not connected
  HC-05 = Bluetooth HC-05

nets (from the schematic view):
  GND: Composant1.GND, 7805.GND, 9_6V_battery.pin1, 12V_from_charge_base.pin2, contacts_to_charge_base.3, 8xAA_2800mA_battery_block.-, SI_4703.GND, to_power_Amp.3, contacts_to_charge_base2.1, R3.Pin_0
  N1: Composant1.D2, SI_4703.!RST
  N2: Composant1.D3, SI_4703.GPIO2
  N3: Composant1.D4, Composant3.RX2_LV
  N4: Composant1.D5, Composant3.RX_LV
  N5: Composant1.A5, Composant3.TX2_HV, 3_3k_2.Pin_1, contacts_to_charge_base3.2
  N6: Composant1.A4, Composant3.TX_HV, 3_3k.Pin_1, contacts_to_charge_base3.1
  N7: Composant1.A2, R3.Pin_1
  N8: Composant1.A0, input_switches.1
  N9: On/OFF_switch.pin1, D1.cathode
  N10: On/OFF_switch.pin2, 12V_Amplifier.pin1, 7805.input_voltage, supply_voltage.1
  5V: 7805.output_voltage, 2200µF.+, 5v_to_3_3V_DC_converter.OUT
  N11: 2200µF.-, 33nF.0
  N12: D1.anode, 12V_from_charge_base.pin1
  N13: Composant3.TX2_LV, SI_4703.SCLK
  N14: Composant3.TX_LV, SI_4703.SDIO
  N15: Composant3.RX_HV, HC-05.TX
  N16: Composant3.RX2_HV, HC-05.RX
  N17: 3_3k.Pin_0, 3_3k_2.Pin_0
  N18: D2.cathode, Q1.C
  N19: D2.anode, Q2.E, 9_6V_battery.pin2, 8xAA_2800mA_battery_block.+
  N20: Q1.E, Q2.B
  N21: Q1.B, Q2.C, R1.Pin_1
  12V: contacts_to_charge_base.1
  N22: contacts_to_charge_base.2, D3.cathode
  N23: SI_4703.FMIP, ANT1.antenna_lead
  N24: SI_4703.ROUT, to_power_Amp.2
  N25: SI_4703.LOUT, to_power_Amp.1
  3.3V: 5v_to_3_3V_DC_converter.IN
  N26: R6.Pin_1, connector_to_front_pannel.2, A0.1

notes:
  FM Radio Main Board
